// Logisim project ALU.circ as structural Verilog: 1 circuit, main circuit main
module main (
  input  [31:0] in_1,
  input  [31:0] in_2,
  input  [4:0] ALU_CONTROL,
  output [31:0] out_4,
  output out_5
);

  wire comparator_1_eq, comparator_1_gt, comparator_1_lt, comparator_2_eq, comparator_2_gt, comparator_2_lt,
       comparator_3_eq, comparator_4_eq, not_1_out, or_2_out, or_3_out;
  wire [31:0] adder_1_out, and_1_out, bit_extender_1_out, bit_extender_2_out, bit_extender_3_out,
       bit_extender_4_out, bit_extender_5_out, bit_extender_6_out, or_1_out, shifter_1_out, shifter_2_out,
       shifter_3_out, subtractor_1_out, xor_1_out;

  Adder #(.width(32)) adder_1 (.a(in_2), .b(in_1), .out(adder_1_out));  // open: cin, cout
  Subtractor #(.width(32)) subtractor_1 (.a(in_2), .b(in_1), .out(subtractor_1_out));  // open: bin, bout
  assign xor_1_out = in_2 ^ in_1;  // XOR_Gate xor_1, 32 bits wide
  assign and_1_out = in_2 & in_1;  // AND_Gate and_1, 32 bits wide
  assign or_1_out = in_2 | in_1;  // OR_Gate or_1, 32 bits wide
  Shifter #(.width(32)) shifter_1 (.in(in_2), .\dist (in_1[4:0]), .out(shifter_1_out));
  Shifter #(.width(32), .shift("lr")) shifter_2 (.in(in_2), .\dist (in_1[4:0]), .out(shifter_2_out));
  Shifter #(.width(32), .shift("ar")) shifter_3 (.in(in_2), .\dist (in_1[4:0]), .out(shifter_3_out));
  Comparator #(.width(32)) comparator_1 (
    .a(in_2), .b(in_1), .gt(comparator_1_gt), .eq(comparator_1_eq), .lt(comparator_1_lt));
  Comparator #(.width(32), .mode("unsigned")) comparator_2 (
    .a(in_2), .b(in_1), .gt(comparator_2_gt), .eq(comparator_2_eq), .lt(comparator_2_lt));
  assign bit_extender_1_out = {{31{1'b0}}, comparator_1_eq};  // Bit_Extender bit_extender_1
  assign bit_extender_2_out = {{31{1'b0}}, comparator_1_lt};  // Bit_Extender bit_extender_2
  assign bit_extender_3_out = {{31{1'b0}}, not_1_out};  // Bit_Extender bit_extender_3
  assign bit_extender_4_out = {{31{1'b0}}, or_2_out};  // Bit_Extender bit_extender_4
  not not_1 (not_1_out, comparator_1_eq);
  or or_2 (or_2_out, comparator_1_gt, comparator_1_eq);
  or or_3 (or_3_out, comparator_2_gt, comparator_2_eq);
  assign bit_extender_5_out = {{31{1'b0}}, or_3_out};  // Bit_Extender bit_extender_5
  assign bit_extender_6_out = {{31{1'b0}}, comparator_2_lt};  // Bit_Extender bit_extender_6
  Multiplexer #(.select(5), .width(32), .enable("false")) multiplexer_1 (
    .in0(adder_1_out), .in1(shifter_1_out), .in2(bit_extender_2_out), .in3(bit_extender_6_out),
    .in4(xor_1_out), .in5(shifter_2_out), .in6(or_1_out), .in7(and_1_out), .in8(subtractor_1_out),
    .in13(shifter_3_out), .in16(bit_extender_1_out), .in17(bit_extender_3_out), .in20(bit_extender_2_out),
    .in21(bit_extender_4_out), .in22(bit_extender_6_out), .in23(bit_extender_5_out), .in31(in_2),
    .out(out_4), .sel(ALU_CONTROL));  // open: in9, in10, in11, in12, in14, in15, in18, in19, in24, in25, in26, in27, in28, in29, in30
  Comparator #(.width(2)) comparator_3 (.a(ALU_CONTROL[4:3]), .b(2'b10), .eq(comparator_3_eq));  // open: gt, lt
  Comparator #(.width(32)) comparator_4 (.a(out_4), .b(32'h1), .eq(comparator_4_eq));  // open: gt, lt
  and and_2 (out_5, comparator_3_eq, comparator_4_eq);

  // Notes on the sheet:
  //   INPUT A
  //   INPUT B
  //   JAL,JALR
  //   XOR,XORI
  //   ADD,ADDI
  //   SUB
  //    AND,ANDI
  //   OR,ORI
  //   SLL ,SLLI
  //   SRL,SRLI
  //   SRA,SRAI
  //   BEQ
  //   SLT,SLTI
  //   BLT
  //   BLTU
  //   BNE
  //   SLTU,SLTIU
  //   BGE
  //   BGEU
  //   OUTPUT
endmodule
