// Logisim project Alu op.circ as structural Verilog: 1 circuit, main circuit main
module main (
  input  R_Type,
  input  Load,
  input  Store,
  input  Branch,
  input  I_Type,
  input  JALR,
  input  JAL,
  input  LUI,
  output [2:0] out_9
);

  wire not_1_out, not_2_out, not_3_out, not_4_out, not_5_out, not_6_out, not_7_out, not_8_out, not_9_out,
       not_10_out, not_11_out, not_12_out, not_13_out;

  not not_1 (not_1_out, R_Type);
  not not_2 (not_2_out, Branch);
  not not_3 (not_3_out, I_Type);
  not not_4 (not_4_out, JALR);
  not not_5 (not_5_out, JAL);
  not not_6 (not_6_out, R_Type);
  not not_7 (not_7_out, Load);
  not not_8 (not_8_out, Store);
  not not_9 (not_9_out, I_Type);
  not not_10 (not_10_out, R_Type);
  not not_11 (not_11_out, Load);
  not not_12 (not_12_out, Branch);
  not not_13 (not_13_out, LUI);
  and and_1 (out_9[2], not_1_out, not_2_out, not_3_out, not_4_out, not_5_out);
  and and_2 (out_9[1], not_6_out, not_7_out, not_8_out, not_9_out);
  and and_3 (out_9[0], not_10_out, not_11_out, not_12_out, not_13_out);
endmodule
