// Logisim project Final Risc-V1 updated.circ as structural Verilog
module riscv_top (
);

  wire and_1_out, button_1_out, button_2_out, clock_1_out, control_unit_1_out_3, control_unit_1_out_5,
       control_unit_1_out_6, control_unit_1_out_7, control_unit_1_out_8, control_unit_1_out_10, main_4_out_5;
  wire [1:0] control_unit_1_out_9, control_unit_1_out_11, control_unit_1_out_12;
  wire [4:0] control_unit_1_out_2;
  wire [19:0] register_1_q_2;
  wire [31:0] adder_1_out, main_1_out_3, main_1_out_4, main_1_out_5, main_1_out_6, main_1_out_7,
       main_2_out_3, main_3_out_8, main_3_out_9, main_4_out_4, multiplexer_1_out, multiplexer_2_out,
       multiplexer_3_out, multiplexer_4_out, multiplexer_5_out, multiplexer_6_out, ram_1_data, register_1_q,
       rom_1_data;

  Clock clock_1 (.out(clock_1_out));
  Adder #(.width(32)) adder_1 (
    .a({register_1_q[31:22], register_1_q_2, register_1_q[1:0]}), .b(32'h4), .out(adder_1_out));  // open: cin, cout
  Register #(.width(32)) register_1 (
    .D(multiplexer_1_out), .Q({register_1_q[31:22], register_1_q_2, register_1_q[1:0]}), .clk(clock_1_out),
    .clr(button_2_out));  // open: en
  Button button_1 (.out(button_1_out));
  Button button_2 (.out(button_2_out));
  ROM #(.addrWidth(20), .dataWidth(32)) rom_1 (.addr(register_1_q_2), .data(rom_1_data));  // open: sel
  Multiplexer #(.select(2), .width(32), .enable("false")) multiplexer_1 (
    .in0(adder_1_out), .in1(multiplexer_3_out), .in2(main_1_out_6), .in3(main_2_out_3),
    .out(multiplexer_1_out), .sel(control_unit_1_out_12));
  Immediate_generation_main main_1 (
    .in_1(rom_1_data), .in_2({register_1_q[31:22], register_1_q_2, register_1_q[1:0]}), .out_3(main_1_out_3),
    .out_4(main_1_out_4), .out_5(main_1_out_5), .out_6(main_1_out_6), .out_7(main_1_out_7));
  Control_Unit control_unit_1 (
    .in_1(rom_1_data), .out_2(control_unit_1_out_2), .out_3(control_unit_1_out_3),
    .out_6(control_unit_1_out_6), .out_7(control_unit_1_out_7), .out_8(control_unit_1_out_8),
    .out_9(control_unit_1_out_9), .out_5(control_unit_1_out_5), .out_10(control_unit_1_out_10),
    .out_11(control_unit_1_out_11), .out_12(control_unit_1_out_12));  // open: out_4
  Multiplexer #(.select(2), .width(32), .enable("false")) multiplexer_2 (
    .in0(main_1_out_7), .in1(main_1_out_5), .in2(main_1_out_3), .in3({32{1'b0}}), .out(multiplexer_2_out),
    .sel(control_unit_1_out_11));
  Multiplexer #(.width(32), .enable("false")) multiplexer_3 (
    .in0(adder_1_out), .in1(main_1_out_4), .out(multiplexer_3_out), .sel(and_1_out));
  Jalr_main main_2 (.in_1(main_3_out_8), .in_2(multiplexer_2_out), .out_3(main_2_out_3));
  REG_updated_main main_3 (
    .in_1(multiplexer_6_out), .in_4(rom_1_data[11:7]), .Clock(clock_1_out), .out_8(main_3_out_8),
    .out_9(main_3_out_9), .in_6(button_1_out), .in_2(control_unit_1_out_7), .in_3(rom_1_data[19:15]),
    .in_5(rom_1_data[24:20]));
  and and_1 (and_1_out, main_4_out_5, control_unit_1_out_5);
  Multiplexer #(.select(2), .width(32), .enable("false")) multiplexer_4 (
    .in0(main_3_out_8), .in1({register_1_q[31:22], register_1_q_2, register_1_q[1:0]}),
    .in2(multiplexer_1_out), .in3(main_3_out_8), .out(multiplexer_4_out), .sel(control_unit_1_out_9));
  Multiplexer #(.width(32), .enable("false")) multiplexer_5 (
    .in0(main_3_out_9), .in1(multiplexer_2_out), .out(multiplexer_5_out), .sel(control_unit_1_out_10));
  Control control_1 ();
  ALU_main main_4 (
    .in_2(multiplexer_4_out), .in_1(multiplexer_5_out), .ALU_CONTROL(control_unit_1_out_2),
    .out_4(main_4_out_4), .out_5(main_4_out_5));
  RAM #(.dataWidth(32), .bus("separate")) ram_1 (
    .addr(main_4_out_4[9:2]), .din(main_3_out_9), .data(ram_1_data), .str(control_unit_1_out_3),
    .clk(clock_1_out), .ld(control_unit_1_out_6));  // open: sel, clr
  Multiplexer #(.width(32), .enable("false")) multiplexer_6 (
    .in0(main_4_out_4), .in1(ram_1_data), .out(multiplexer_6_out), .sel(control_unit_1_out_8));

  // Notes on the sheet:
  //   CLock
  //   Restart Program
  //   Reset
  //   contents of rom_1 (hex, n*v repeats v):
  //   533 5b3 1400613 c5de63 259693 8686b3 6a703 e50533 158593 fe9ff06f
endmodule

module Type_decode (
  input  [6:0] in_1,
  output out_2,
  output out_3,
  output out_4,
  output out_5,
  output out_6,
  output out_7,
  output out_8,
  output out_9
);

  Comparator #(.width(7), .mode("unsigned")) comparator_1 (.a(in_1), .b(7'b0110011), .eq(out_2));  // open: gt, lt
  Comparator #(.width(7), .mode("unsigned")) comparator_2 (.a(in_1), .b(7'b0000011), .eq(out_3));  // open: gt, lt
  Comparator #(.width(7), .mode("unsigned")) comparator_3 (.a(in_1), .b(7'b0100011), .eq(out_4));  // open: gt, lt
  Comparator #(.width(7), .mode("unsigned")) comparator_4 (.a(in_1), .b(7'b1100011), .eq(out_5));  // open: gt, lt
  Comparator #(.width(7), .mode("unsigned")) comparator_5 (.a(in_1), .b(7'b0010011), .eq(out_6));  // open: gt, lt
  Comparator #(.width(7), .mode("unsigned")) comparator_6 (.a(in_1), .b(7'b0110111), .eq(out_7));  // open: gt, lt
  Comparator #(.width(7), .mode("unsigned")) comparator_7 (.a(in_1), .b(7'b1101111), .eq(out_8));  // open: gt, lt
  Comparator #(.width(7), .mode("unsigned")) comparator_8 (.a(in_1), .b(7'b0110111), .eq(out_9));  // open: gt, lt
  Control control_1 ();
endmodule

module Control_Unit (
  input  [31:0] in_1,
  output [4:0] out_2,
  output out_3,
  output [6:0] out_4,
  output out_5,
  output out_6,
  output out_7,
  output out_8,
  output [1:0] out_9,
  output out_10,
  output [1:0] out_11,
  output [1:0] out_12
);

  wire type_decode_1_out_2, type_decode_1_out_3, type_decode_1_out_4, type_decode_1_out_5,
       type_decode_1_out_6, type_decode_1_out_7, type_decode_1_out_8, type_decode_1_out_9;

  Control control_1 ();
  Type_decode type_decode_1 (
    .in_1(in_1[6:0]), .out_2(type_decode_1_out_2), .out_3(type_decode_1_out_3), .out_4(type_decode_1_out_4),
    .out_5(type_decode_1_out_5), .out_6(type_decode_1_out_6), .out_7(type_decode_1_out_7),
    .out_8(type_decode_1_out_8), .out_9(type_decode_1_out_9));
  Control control_2 ();
  CU1 cu1_1 (
    .R_type(type_decode_1_out_2), .Load(type_decode_1_out_3), .Store(type_decode_1_out_4),
    .Branch(type_decode_1_out_5), .I_Type(type_decode_1_out_6), .JALR(type_decode_1_out_7),
    .JAL(type_decode_1_out_8), .Lui(type_decode_1_out_9), .MEM_Write(out_3), .Branch_2(out_5),
    .MEM_READ(out_6), .REGWRITE(out_7), .MEMTOREG(out_8), .out_14(out_9), .operand_B_sel(out_10),
    .out_16(out_11), .out_17(out_12));
  AlUcontrol alucontrol_1 (
    .R_type(type_decode_1_out_2), .Load(type_decode_1_out_3), .Store(type_decode_1_out_4),
    .Branch(type_decode_1_out_5), .I_Type(type_decode_1_out_6), .JALR(type_decode_1_out_7),
    .JAL(type_decode_1_out_8), .Lui(type_decode_1_out_9), .func7(in_1[30]), .out_11(out_2),
    .in_10(in_1[14:12]));

  assign out_4 = in_1[6:0];
endmodule

module CU1 (
  input  R_type,
  input  Load,
  input  Store,
  input  Branch,
  input  I_Type,
  input  JALR,
  input  JAL,
  input  Lui,
  output MEM_Write,
  output Branch_2,
  output MEM_READ,
  output REGWRITE,
  output MEMTOREG,
  output [1:0] out_14,
  output operand_B_sel,
  output [1:0] out_16,
  output [1:0] out_17
);

  wire and_1_out, and_2_out, and_3_out, not_1_out, not_2_out, not_3_out, not_4_out, not_5_out, not_6_out,
       not_7_out, not_8_out, not_9_out, not_10_out;

  not not_1 (not_1_out, Store);
  and and_1 (and_1_out, not_1_out, not_2_out, JAL);
  not not_2 (not_2_out, Branch);
  not not_3 (not_3_out, Load);
  not not_4 (not_4_out, Store);
  not not_5 (not_5_out, Branch);
  not not_6 (not_6_out, I_Type);
  or or_1 (operand_B_sel, Lui, I_Type, Store, Load);
  or or_2 (out_17[0], JALR, Branch);
  not not_7 (not_7_out, Load);
  not not_8 (not_8_out, Store);
  not not_9 (not_9_out, Branch);
  not not_10 (not_10_out, I_Type);
  or or_3 (out_14[1], Lui, and_2_out, JALR);
  and and_2 (and_2_out, not_3_out, not_4_out, not_5_out, not_6_out, JAL);
  and and_3 (and_3_out, not_7_out, not_8_out, not_9_out, not_10_out, JAL);
  or or_4 (out_17[1], and_3_out, JALR);
  or or_5 (REGWRITE, Lui, and_1_out, JALR, I_Type, Load, R_type);

  assign Branch_2 = Branch;
  assign MEM_READ = Load;
  assign MEM_Write = Store;
  assign MEMTOREG = Load;
  assign out_14[0] = Lui;
  assign out_16 = {Store, Lui};
endmodule

module AlUcontrol (
  input  R_type,
  input  Load,
  input  Store,
  input  Branch,
  input  I_Type,
  input  JALR,
  input  JAL,
  input  Lui,
  input  func7,
  input  [2:0] in_10,
  output [4:0] out_11
);

  wire [2:0] main_1_out_9;

  Alu_op_main main_1 (
    .R_Type(R_type), .Load(Load), .Store(Store), .Branch(Branch), .I_Type(I_Type), .JALR(JALR), .JAL(JAL),
    .LUI(Lui), .out_9(main_1_out_9));
  control_op_main main_2 (.out_4(out_11), .ALUOp(main_1_out_9), .Func_7(func7), .Func_3(in_10));
endmodule
