// Logisim project Sid_Alu.circ as structural Verilog: 12 circuits, main circuit ALU
module _1_bit_adder (
  input  a,
  input  b,
  input  cin,
  output sum,
  output cout
);

  wire and_1_out, and_2_out, xor_1_out;

  xor xor_1 (xor_1_out, a, b);
  and and_1 (and_1_out, a, b);
  and and_2 (and_2_out, cin, xor_1_out);
  xor xor_2 (sum, xor_1_out, cin);
  or or_1 (cout, and_2_out, and_1_out);
endmodule

module _1_bit_subtractor (
  input  a,
  input  b,
  input  borrowin,
  output diff,
  output borrowout
);

  wire and_1_out, and_2_out, not_1_out, not_2_out, xor_1_out;

  not not_1 (not_1_out, a);
  xor xor_1 (xor_1_out, a, b);
  not not_2 (not_2_out, xor_1_out);
  and and_1 (and_1_out, not_1_out, b);
  and and_2 (and_2_out, borrowin, not_2_out);
  xor xor_2 (diff, xor_1_out, borrowin);
  or or_1 (borrowout, and_2_out, and_1_out);
endmodule

module ALU (
  input  Cin,
  input  [31:0] a,
  input  s1,
  input  [31:0] b,
  input  B_in,
  input  s0,
  output Cout,
  output [31:0] \output ,
  output B_out
);

  wire [31:0] and_1_out, multiplexer_1_out, multiplexer_2_out, n32_bit_adder_1_sum,
       n32_bit_subtractor_1_diff, or_1_out;

  _32_bit_adder u_32_bit_adder_1 (.cin(Cin), .a(a), .b(b), .sum(n32_bit_adder_1_sum), .cout(Cout));
  assign and_1_out = a & b;  // AND_Gate and_1, 32 bits wide
  _32_bit_subtractor u_32_bit_subtractor_1 (
    .borrowin(B_in), .a(a), .b(b), .diff(n32_bit_subtractor_1_diff), .borrowout(B_out));
  assign or_1_out = a | b;  // OR_Gate or_1, 32 bits wide
  Multiplexer #(.width(32)) multiplexer_1 (
    .in0(n32_bit_adder_1_sum), .in1(and_1_out), .out(multiplexer_1_out), .sel(s0));  // open: en
  Multiplexer #(.width(32)) multiplexer_2 (
    .in0(n32_bit_subtractor_1_diff), .in1(or_1_out), .out(multiplexer_2_out), .sel(s0));  // open: en
  Multiplexer #(.width(32)) multiplexer_3 (
    .in0(multiplexer_1_out), .in1(multiplexer_2_out), .out(\output ), .sel(s1));  // open: en
endmodule

module _8_bit_adder (
  input  cin,
  input  [7:0] in_2,
  input  [7:0] in_3,
  output [7:0] out_4,
  output cout
);

  wire n1_bit_adder_1_cout, n1_bit_adder_2_cout, n1_bit_adder_3_cout, n1_bit_adder_4_cout,
       n1_bit_adder_5_cout, n1_bit_adder_6_cout, n1_bit_adder_7_cout;

  _1_bit_adder u_1_bit_adder_1 (.a(in_2[0]), .b(in_3[0]), .cin(cin), .sum(out_4[0]), .cout(n1_bit_adder_1_cout));
  _1_bit_adder u_1_bit_adder_2 (
    .a(in_2[1]), .b(in_3[1]), .cin(n1_bit_adder_1_cout), .sum(out_4[1]), .cout(n1_bit_adder_2_cout));
  _1_bit_adder u_1_bit_adder_3 (
    .a(in_2[2]), .b(in_3[2]), .cin(n1_bit_adder_2_cout), .sum(out_4[2]), .cout(n1_bit_adder_3_cout));
  _1_bit_adder u_1_bit_adder_4 (
    .a(in_2[3]), .b(in_3[3]), .cin(n1_bit_adder_3_cout), .sum(out_4[3]), .cout(n1_bit_adder_4_cout));
  _1_bit_adder u_1_bit_adder_5 (
    .a(in_2[4]), .b(in_3[4]), .cin(n1_bit_adder_4_cout), .sum(out_4[4]), .cout(n1_bit_adder_5_cout));
  _1_bit_adder u_1_bit_adder_6 (
    .a(in_2[5]), .b(in_3[5]), .cin(n1_bit_adder_5_cout), .sum(out_4[5]), .cout(n1_bit_adder_6_cout));
  _1_bit_adder u_1_bit_adder_7 (
    .a(in_2[6]), .b(in_3[6]), .cin(n1_bit_adder_6_cout), .sum(out_4[6]), .cout(n1_bit_adder_7_cout));
  _1_bit_adder u_1_bit_adder_8 (.a(in_2[7]), .b(in_2[7]), .cin(n1_bit_adder_7_cout), .sum(out_4[7]), .cout(cout));

  assign in_3[7] = in_2[7];
endmodule

module _32_bit_adder (
  input  cin,
  input  [31:0] a,
  input  [31:0] b,
  output [31:0] sum,
  output cout
);

  wire n8_bit_adder_1_cout, n8_bit_adder_2_cout, n8_bit_adder_3_cout;

  _8_bit_adder u_8_bit_adder_1 (.cin(cin), .in_2(a[7:0]), .in_3(b[7:0]), .out_4(sum[7:0]), .cout(n8_bit_adder_1_cout));
  _8_bit_adder u_8_bit_adder_2 (
    .cin(n8_bit_adder_1_cout), .in_2(a[15:8]), .in_3(b[15:8]), .out_4(sum[15:8]), .cout(n8_bit_adder_2_cout));
  _8_bit_adder u_8_bit_adder_3 (
    .cin(n8_bit_adder_2_cout), .in_2(a[23:16]), .in_3(b[23:16]), .out_4(sum[23:16]),
    .cout(n8_bit_adder_3_cout));
  _8_bit_adder u_8_bit_adder_4 (
    .cin(n8_bit_adder_3_cout), .in_2(a[31:24]), .in_3(b[31:24]), .out_4(sum[31:24]), .cout(cout));
endmodule

module _32_bit_subtractor (
  input  borrowin,
  input  [31:0] a,
  input  [31:0] b,
  output [31:0] diff,
  output borrowout
);

  wire n8_bit_subtractor_1_borrowout, n8_bit_subtractor_2_borrowout, n8_bit_subtractor_3_borrowout;

  _8_bit_subtractor u_8_bit_subtractor_1 (
    .borrowin(borrowin), .in_2(a[7:0]), .in_3(b[7:0]), .out_4(diff[7:0]),
    .borrowout(n8_bit_subtractor_1_borrowout));
  _8_bit_subtractor u_8_bit_subtractor_2 (
    .borrowin(n8_bit_subtractor_1_borrowout), .in_2(a[15:8]), .in_3(b[15:8]), .out_4(diff[15:8]),
    .borrowout(n8_bit_subtractor_2_borrowout));
  _8_bit_subtractor u_8_bit_subtractor_3 (
    .borrowin(n8_bit_subtractor_2_borrowout), .in_2(a[23:16]), .in_3(b[23:16]), .out_4(diff[23:16]),
    .borrowout(n8_bit_subtractor_3_borrowout));
  _8_bit_subtractor u_8_bit_subtractor_4 (
    .borrowin(n8_bit_subtractor_3_borrowout), .in_2(a[31:24]), .in_3(b[31:24]), .out_4(diff[31:24]),
    .borrowout(borrowout));
endmodule

module _8_bit_subtractor (
  input  borrowin,
  input  [7:0] in_2,
  input  [7:0] in_3,
  output [7:0] out_4,
  output borrowout
);

  wire n1_bit_subtractor_1_borrowout, n1_bit_subtractor_2_borrowout, n1_bit_subtractor_3_borrowout,
       n1_bit_subtractor_4_borrowout, n1_bit_subtractor_5_borrowout, n1_bit_subtractor_6_borrowout,
       n1_bit_subtractor_7_borrowout;

  _1_bit_subtractor u_1_bit_subtractor_1 (
    .a(in_2[0]), .b(in_3[0]), .borrowin(borrowin), .diff(out_4[0]), .borrowout(n1_bit_subtractor_1_borrowout));
  _1_bit_subtractor u_1_bit_subtractor_2 (
    .a(in_2[1]), .b(in_3[1]), .borrowin(n1_bit_subtractor_1_borrowout), .diff(out_4[1]),
    .borrowout(n1_bit_subtractor_2_borrowout));
  _1_bit_subtractor u_1_bit_subtractor_3 (
    .a(in_2[2]), .b(in_3[2]), .borrowin(n1_bit_subtractor_2_borrowout), .diff(out_4[2]),
    .borrowout(n1_bit_subtractor_3_borrowout));
  _1_bit_subtractor u_1_bit_subtractor_4 (
    .a(in_2[3]), .b(in_3[3]), .borrowin(n1_bit_subtractor_3_borrowout), .diff(out_4[3]),
    .borrowout(n1_bit_subtractor_4_borrowout));
  _1_bit_subtractor u_1_bit_subtractor_5 (
    .a(in_2[4]), .b(in_3[4]), .borrowin(n1_bit_subtractor_4_borrowout), .diff(out_4[4]),
    .borrowout(n1_bit_subtractor_5_borrowout));
  _1_bit_subtractor u_1_bit_subtractor_6 (
    .a(in_2[5]), .b(in_3[5]), .borrowin(n1_bit_subtractor_5_borrowout), .diff(out_4[5]),
    .borrowout(n1_bit_subtractor_6_borrowout));
  _1_bit_subtractor u_1_bit_subtractor_7 (
    .a(in_2[6]), .b(in_3[6]), .borrowin(n1_bit_subtractor_6_borrowout), .diff(out_4[6]),
    .borrowout(n1_bit_subtractor_7_borrowout));
  _1_bit_subtractor u_1_bit_subtractor_8 (
    .a(in_2[7]), .b(in_3[7]), .borrowin(n1_bit_subtractor_7_borrowout), .diff(out_4[7]), .borrowout(borrowout));
endmodule

module datapath (
  input  in_1,
  input  C_in,
  input  B_in,
  input  [7:0] in_4,
  input  [4:0] in_5,
  input  regWriteEnable,
  input  B_sel,
  input  ALU_sel,
  output [31:0] value_rd,
  output C_out,
  output B_out,
  output [6:0] op_code,
  output [2:0] func3,
  output [6:0] out_14
);

  wire clock_1_out;
  wire [7:0] adder_1_out, counter_1_q;
  wire [24:7] rom_1_data;
  wire [31:0] bit_extender_1_out, multiplexer_1_out, REG_FILE_value_rs1, REG_FILE_value_rs2;

  Clock clock_1 (.out(clock_1_out));
  Counter counter_1 (.D(adder_1_out), .Q(counter_1_q), .clk(clock_1_out));  // open: load, count, carry, clr
  Adder adder_1 (.a(in_4), .b(counter_1_q), .out(adder_1_out));  // open: cin, cout
  ROM #(.dataWidth(32)) rom_1 (
    .addr(counter_1_q), .data({out_14, rom_1_data[24:15], func3, rom_1_data[11:7], op_code}));  // open: sel
  assign bit_extender_1_out = {{20{1'b0}}, {out_14, rom_1_data[24:20]}};  // Bit_Extender bit_extender_1
  Register_file_32_bits REG_FILE (
    .value_rd(value_rd), .value_rs1(REG_FILE_value_rs1), .value_rs2(REG_FILE_value_rs2),
    .rd(rom_1_data[11:7]), .clk(clock_1_out), .regWriteEnable(regWriteEnable), .read_rs1(rom_1_data[19:15]),
    .read_rs2(rom_1_data[24:20]));
  Multiplexer #(.width(32), .enable("false")) multiplexer_1 (
    .in0(REG_FILE_value_rs2), .in1(bit_extender_1_out), .out(multiplexer_1_out), .sel(B_sel));
  // ALU_R___I_type alu_r_i_type_1: pin names not known; wires that end beside it: C_in, B_in, in_5, REG_FILE_value_rs1
  Bit_Extender #(.in_width(7), .out_width(1)) bit_extender_2 (.in(out_14), .out(ALU_sel));
  Register_file_32_bits register_file_32_bits_1 ();  // open: value_rd, value_rs1, value_rs2, rd, clk, regWriteEnable, read_rs1, read_rs2

  // Notes on the sheet:
  //   contents of rom_1 (hex, n*v repeats v):
  //   500213 600293 40428333
  //   imm[20:31]
  //   value_rd
  //   rs1
  //   rs2
  //   rd
  //   value_rs1
  //   value_rs2
  //   reg_mem
endmodule

module Register_file_32_bits (
  input  clk,
  input  [4:0] read_rs1,
  input  [4:0] rd,
  input  [4:0] read_rs2,
  input  regWriteEnable,
  input  [31:0] value_rd,
  output [31:0] value_rs1,
  output [31:0] value_rs2
);

  wire and_1_out, and_2_out, and_3_out, and_4_out, and_5_out, and_6_out, and_7_out, and_8_out, and_9_out,
       and_10_out, and_11_out, and_12_out, and_13_out, and_14_out, and_15_out, and_16_out, and_17_out,
       and_18_out, and_19_out, and_20_out, and_21_out, and_22_out, and_23_out, and_24_out, and_25_out,
       and_26_out, and_27_out, and_28_out, and_29_out, and_30_out, and_31_out, and_32_out, decoder_1_out0,
       decoder_1_out1, decoder_1_out2, decoder_1_out3, decoder_1_out4, decoder_1_out5, decoder_1_out6,
       decoder_1_out7, decoder_1_out8, decoder_1_out9, decoder_1_out10, decoder_1_out11, decoder_1_out12,
       decoder_1_out13, decoder_1_out14, decoder_1_out15, decoder_1_out16, decoder_1_out17, decoder_1_out18,
       decoder_1_out19, decoder_1_out20, decoder_1_out21, decoder_1_out22, decoder_1_out23, decoder_1_out24,
       decoder_1_out25, decoder_1_out26, decoder_1_out27, decoder_1_out28, decoder_1_out29, decoder_1_out30,
       decoder_1_out31, undriven, undriven_2;
  wire [31:0] register_1_q, register_2_q, register_3_q, register_4_q, register_5_q, register_6_q,
       register_7_q, register_8_q, register_9_q, register_10_q, register_11_q, register_12_q, register_13_q,
       register_14_q, register_15_q, register_16_q, register_17_q, register_18_q, register_19_q,
       register_20_q, register_21_q, register_22_q, register_23_q, register_24_q, register_25_q,
       register_26_q, register_27_q, register_28_q, register_29_q, register_30_q, register_31_q,
       register_32_q;

  Decoder #(.select(5), .enable("false")) decoder_1 (
    .out0(decoder_1_out0), .out1(decoder_1_out1), .out2(decoder_1_out2), .out3(decoder_1_out3),
    .out4(decoder_1_out4), .out5(decoder_1_out5), .out6(decoder_1_out6), .out7(decoder_1_out7),
    .out8(decoder_1_out8), .out9(decoder_1_out9), .out10(decoder_1_out10), .out11(decoder_1_out11),
    .out12(decoder_1_out12), .out13(decoder_1_out13), .out14(decoder_1_out14), .out15(decoder_1_out15),
    .out16(decoder_1_out16), .out17(decoder_1_out17), .out18(decoder_1_out18), .out19(decoder_1_out19),
    .out20(decoder_1_out20), .out21(decoder_1_out21), .out22(decoder_1_out22), .out23(decoder_1_out23),
    .out24(decoder_1_out24), .out25(decoder_1_out25), .out26(decoder_1_out26), .out27(decoder_1_out27),
    .out28(decoder_1_out28), .out29(decoder_1_out29), .out30(decoder_1_out30), .out31(decoder_1_out31),
    .sel(rd));
  and and_1 (and_1_out, decoder_1_out0, regWriteEnable);
  and and_2 (and_2_out, decoder_1_out1, regWriteEnable);
  and and_3 (and_3_out, decoder_1_out2, regWriteEnable);
  and and_4 (and_4_out, decoder_1_out3, regWriteEnable);
  and and_5 (and_5_out, decoder_1_out4, regWriteEnable);
  and and_6 (and_6_out, decoder_1_out5, regWriteEnable);
  and and_7 (and_7_out, decoder_1_out6, regWriteEnable);
  and and_8 (and_8_out, decoder_1_out7, regWriteEnable);
  and and_9 (and_9_out, decoder_1_out8, regWriteEnable);
  and and_10 (and_10_out, decoder_1_out9, regWriteEnable);
  and and_11 (and_11_out, decoder_1_out10, regWriteEnable);
  and and_12 (and_12_out, decoder_1_out11, regWriteEnable);
  and and_13 (and_13_out, decoder_1_out12, regWriteEnable);
  and and_14 (and_14_out, decoder_1_out13, regWriteEnable);
  and and_15 (and_15_out, decoder_1_out14, regWriteEnable);
  and and_16 (and_16_out, decoder_1_out15, regWriteEnable);
  and and_17 (and_17_out, decoder_1_out16, regWriteEnable);
  and and_18 (and_18_out, decoder_1_out17, regWriteEnable);
  and and_19 (and_19_out, decoder_1_out18, regWriteEnable);
  and and_20 (and_20_out, decoder_1_out19, regWriteEnable);
  and and_21 (and_21_out, decoder_1_out20, regWriteEnable);
  and and_22 (and_22_out, decoder_1_out21, regWriteEnable);
  and and_23 (and_23_out, decoder_1_out22, regWriteEnable);
  and and_24 (and_24_out, decoder_1_out23, regWriteEnable);
  and and_25 (and_25_out, decoder_1_out24, regWriteEnable);
  and and_26 (and_26_out, decoder_1_out25, regWriteEnable);
  and and_27 (and_27_out, decoder_1_out26, regWriteEnable);
  and and_28 (and_28_out, decoder_1_out27, regWriteEnable);
  and and_29 (and_29_out, decoder_1_out28, regWriteEnable);
  and and_30 (and_30_out, decoder_1_out29, regWriteEnable);
  and and_31 (and_31_out, decoder_1_out30, regWriteEnable);
  and and_32 (and_32_out, decoder_1_out31, regWriteEnable);
  Register #(.width(32)) register_1 (.D(value_rd), .en(undriven_2), .Q(register_1_q), .clk(clk), .clr(and_1_out));
  Register #(.width(32)) register_2 (.D(value_rd), .en(undriven_2), .Q(register_2_q), .clk(clk), .clr(and_2_out));
  Register #(.width(32)) register_3 (.D(value_rd), .en(undriven_2), .Q(register_3_q), .clk(and_3_out), .clr(clk));
  Register #(.width(32)) register_4 (.D(value_rd), .en(undriven_2), .Q(register_4_q), .clk(clk), .clr(and_4_out));
  Register #(.width(32)) register_5 (.D(value_rd), .en(undriven_2), .Q(register_5_q), .clk(clk), .clr(and_5_out));
  Register #(.width(32)) register_6 (.D(value_rd), .en(undriven_2), .Q(register_6_q), .clk(clk), .clr(and_6_out));
  Register #(.width(32)) register_7 (.D(value_rd), .en(undriven_2), .Q(register_7_q), .clk(clk), .clr(and_7_out));
  Register #(.width(32)) register_8 (.D(value_rd), .en(undriven_2), .Q(register_8_q), .clk(clk), .clr(and_8_out));
  Register #(.width(32)) register_9 (.D(value_rd), .en(undriven_2), .Q(register_9_q), .clk(clk), .clr(and_9_out));
  Register #(.width(32)) register_10 (.D(value_rd), .en(undriven_2), .Q(register_10_q), .clk(clk), .clr(and_10_out));
  Register #(.width(32)) register_11 (.D(value_rd), .en(undriven_2), .Q(register_11_q), .clk(clk), .clr(and_11_out));
  Register #(.width(32)) register_12 (.D(value_rd), .en(undriven_2), .Q(register_12_q), .clk(clk), .clr(and_12_out));
  Register #(.width(32)) register_13 (.D(value_rd), .en(undriven_2), .Q(register_13_q), .clk(clk), .clr(and_13_out));
  Register #(.width(32)) register_14 (.D(value_rd), .en(undriven_2), .Q(register_14_q), .clk(clk), .clr(and_14_out));
  Register #(.width(32)) register_15 (.D(value_rd), .en(undriven_2), .Q(register_15_q), .clk(clk), .clr(and_15_out));
  Register #(.width(32)) register_16 (.D(value_rd), .en(undriven), .Q(register_16_q), .clk(clk), .clr(and_16_out));
  Register #(.width(32)) register_17 (.D(value_rd), .Q(register_17_q), .clk(clk), .clr(and_17_out));  // open: en
  Register #(.width(32)) register_18 (.D(value_rd), .Q(register_18_q), .clk(clk), .clr(and_18_out));  // open: en
  Register #(.width(32)) register_19 (.D(value_rd), .Q(register_19_q), .clk(clk), .clr(and_19_out));  // open: en
  Register #(.width(32)) register_20 (.D(value_rd), .Q(register_20_q), .clk(clk), .clr(and_20_out));  // open: en
  Register #(.width(32)) register_21 (.D(value_rd), .Q(register_21_q), .clk(clk), .clr(and_21_out));  // open: en
  Register #(.width(32)) register_22 (.D(value_rd), .Q(register_22_q), .clk(clk), .clr(and_22_out));  // open: en
  Register #(.width(32)) register_23 (.D(value_rd), .Q(register_23_q), .clk(clk), .clr(and_23_out));  // open: en
  Register #(.width(32)) register_24 (.D(value_rd), .Q(register_24_q), .clk(clk), .clr(and_24_out));  // open: en
  Register #(.width(32)) register_25 (.D(value_rd), .Q(register_25_q), .clk(clk), .clr(and_25_out));  // open: en
  Register #(.width(32)) register_26 (.D(value_rd), .Q(register_26_q), .clk(clk), .clr(and_26_out));  // open: en
  Register #(.width(32)) register_27 (.D(value_rd), .Q(register_27_q), .clk(clk), .clr(and_27_out));  // open: en
  Register #(.width(32)) register_28 (.D(value_rd), .Q(register_28_q), .clk(clk), .clr(and_28_out));  // open: en
  Register #(.width(32)) register_29 (.D(value_rd), .Q(register_29_q), .clk(clk), .clr(and_29_out));  // open: en
  Register #(.width(32)) register_30 (.D(value_rd), .Q(register_30_q), .clk(clk), .clr(and_30_out));  // open: en
  Register #(.width(32)) register_31 (.D(value_rd), .Q(register_31_q), .clk(clk), .clr(and_31_out));  // open: en
  Register #(.width(32)) register_32 (.D(value_rd), .en(undriven_2), .Q(register_32_q), .clk(clk), .clr(and_32_out));
  Multiplexer #(.select(5), .width(32), .enable("false")) multiplexer_1 (
    .in0(register_1_q), .in1(register_2_q), .in2(register_3_q), .in3(register_4_q), .in4(register_5_q),
    .in5(register_6_q), .in6(register_7_q), .in7(register_8_q), .in8(register_9_q), .in9(register_10_q),
    .in10(register_11_q), .in11(register_12_q), .in12(register_13_q), .in13(register_14_q),
    .in14(register_15_q), .in15(register_16_q), .in16(register_17_q), .in17(register_18_q),
    .in18(register_19_q), .in19(register_20_q), .in20(register_21_q), .in21(register_22_q),
    .in22(register_23_q), .in23(register_24_q), .in24(register_25_q), .in25(register_26_q),
    .in26(register_27_q), .in27(register_28_q), .in28(register_29_q), .in29(register_30_q),
    .in30(register_31_q), .in31(register_32_q), .out(value_rs1), .sel(read_rs1));
  Multiplexer #(.select(5), .width(32), .enable("false")) multiplexer_2 (
    .in0(register_1_q), .in1(register_2_q), .in2(register_3_q), .in3(register_4_q), .in4(register_5_q),
    .in5(register_6_q), .in6(register_7_q), .in7(register_8_q), .in8(register_9_q), .in9(register_10_q),
    .in10(register_11_q), .in11(register_12_q), .in12(register_13_q), .in13(register_14_q),
    .in14(register_15_q), .in15(register_16_q), .in16(register_17_q), .in17(register_18_q),
    .in18(register_19_q), .in19(register_20_q), .in20(register_21_q), .in21(register_22_q),
    .in22(register_23_q), .in23(register_24_q), .in24(register_25_q), .in25(register_26_q),
    .in26(register_27_q), .in27(register_28_q), .in28(register_29_q), .in29(register_30_q),
    .in30(register_31_q), .in31(register_32_q), .out(value_rs2), .sel(read_rs2));
endmodule

module ALU_Branch (
  input  Cin,
  input  B_in,
  input  ALU_sel,
  input  [4:0] reg_mem,
  input  [31:0] a,
  input  [2:0] func3,
  input  [31:0] b,
  output Cout,
  output Bout,
  output [31:0] \output 
);

  wire comparator_1_lt, comparator_2_lt;
  wire [31:0] and_1_out, bit_extender_1_out, bit_extender_2_out, multiplexer_1_out, multiplexer_2_out,
       n32_bit_adder_1_sum, n32_bit_subtractor_1_diff, or_1_out, shifter_1_out, shifter_2_out, shifter_3_out,
       xor_1_out;

  _32_bit_adder u_32_bit_adder_1 (.cin(Cin), .a(a), .b(b), .sum(n32_bit_adder_1_sum), .cout(Cout));
  _32_bit_subtractor u_32_bit_subtractor_1 (
    .borrowin(B_in), .a(a), .b(b), .diff(n32_bit_subtractor_1_diff), .borrowout(Bout));
  Shifter #(.width(32)) shifter_1 (.in(a), .\dist (reg_mem), .out(shifter_1_out));
  Comparator #(.width(32)) comparator_1 (.a(a), .b(b), .lt(comparator_1_lt));  // open: gt, eq
  Comparator #(.width(32), .mode("unsigned")) comparator_2 (.a(a), .b(b), .lt(comparator_2_lt));  // open: gt, eq
  assign xor_1_out = a ^ b;  // XOR_Gate xor_1, 32 bits wide
  Shifter #(.width(32), .shift("lr")) shifter_2 (.in(a), .\dist (reg_mem), .out(shifter_2_out));
  Shifter #(.width(32), .shift("ar")) shifter_3 (.in(a), .\dist (reg_mem), .out(shifter_3_out));
  assign or_1_out = a | b;  // OR_Gate or_1, 32 bits wide
  assign and_1_out = a & b;  // AND_Gate and_1, 32 bits wide
  Multiplexer #(.width(32), .enable("false")) multiplexer_1 (
    .in0(n32_bit_adder_1_sum), .in1(n32_bit_subtractor_1_diff), .out(multiplexer_1_out), .sel(ALU_sel));
  assign bit_extender_1_out = {{31{1'b0}}, comparator_1_lt};  // Bit_Extender bit_extender_1
  assign bit_extender_2_out = {{31{1'b0}}, comparator_2_lt};  // Bit_Extender bit_extender_2
  Multiplexer #(.width(32), .enable("false")) multiplexer_2 (
    .in0(shifter_2_out), .in1(shifter_3_out), .out(multiplexer_2_out), .sel(ALU_sel));
  Multiplexer #(.select(3), .width(32), .enable("false")) multiplexer_3 (
    .in0(multiplexer_1_out), .in1(shifter_1_out), .in2(bit_extender_1_out), .in3(bit_extender_2_out),
    .in4(xor_1_out), .in5(multiplexer_2_out), .in6(or_1_out), .in7(and_1_out), .out(\output ), .sel(func3));
endmodule

module ALU_R___I_type (
  input  Cin,
  input  B_in,
  input  [31:0] a,
  input  [31:0] b,
  input  [3:0] ALu_Controller,
  output Cout,
  output Bout,
  output [31:0] \output 
);

  wire comparator_1_lt, comparator_2_lt;
  wire [31:0] and_1_out, bit_extender_1_out, bit_extender_2_out, n32_bit_adder_1_sum,
       n32_bit_subtractor_1_diff, or_1_out, shifter_1_out, shifter_2_out, shifter_3_out, xor_1_out;

  _32_bit_adder u_32_bit_adder_1 (.cin(Cin), .a(a), .b(b), .sum(n32_bit_adder_1_sum), .cout(Cout));
  _32_bit_subtractor u_32_bit_subtractor_1 (
    .borrowin(B_in), .a(a), .b(b), .diff(n32_bit_subtractor_1_diff), .borrowout(Bout));
  Shifter #(.width(32)) shifter_1 (.in(a), .\dist (b[4:0]), .out(shifter_1_out));
  Comparator #(.width(32)) comparator_1 (.a(a), .b(b), .lt(comparator_1_lt));  // open: gt, eq
  Comparator #(.width(32), .mode("unsigned")) comparator_2 (.a(a), .b(b), .lt(comparator_2_lt));  // open: gt, eq
  assign xor_1_out = a ^ b;  // XOR_Gate xor_1, 32 bits wide
  Shifter #(.width(32), .shift("lr")) shifter_2 (.in(a), .\dist (b[4:0]), .out(shifter_2_out));
  Shifter #(.width(32), .shift("ar")) shifter_3 (.in(a), .\dist (b[4:0]), .out(shifter_3_out));
  assign or_1_out = a | b;  // OR_Gate or_1, 32 bits wide
  assign and_1_out = a & b;  // AND_Gate and_1, 32 bits wide
  assign bit_extender_1_out = {{31{1'b0}}, comparator_1_lt};  // Bit_Extender bit_extender_1
  assign bit_extender_2_out = {{31{1'b0}}, comparator_2_lt};  // Bit_Extender bit_extender_2
  Multiplexer #(.select(4), .width(32), .enable("false")) multiplexer_1 (
    .in0(n32_bit_adder_1_sum), .in1(shifter_1_out), .in2(bit_extender_1_out), .in3(bit_extender_2_out),
    .in4(xor_1_out), .in5(shifter_2_out), .in6(shifter_3_out), .in7(or_1_out), .in8(and_1_out),
    .in9(n32_bit_subtractor_1_diff), .out(\output ), .sel(ALu_Controller));  // open: in10, in11, in12, in13, in14, in15
endmodule

module xyz (
  input  in_1,
  input  C_in,
  input  [7:0] in_3,
  input  B_in,
  input  [4:0] reg_mem,
  input  regWriteEnable,
  input  B_sel,
  input  ALU_sel,
  output [31:0] value_rd,
  output C_out,
  output B_out,
  output [6:0] op_code,
  output [2:0] func3,
  output [6:0] out_14
);

  wire bit_extender_2_out, clock_1_out, REG_FILE_p8;
  wire [7:0] adder_1_out, counter_1_q;
  wire [24:7] rom_1_data;
  wire [31:0] bit_extender_1_out, multiplexer_1_out, REG_FILE_p9;

  Clock clock_1 (.out(clock_1_out));
  Counter counter_1 (.D(adder_1_out), .Q(counter_1_q), .clk(clock_1_out));  // open: load, count, carry, clr
  Adder adder_1 (.a(in_3), .b(counter_1_q), .out(adder_1_out));  // open: cin, cout
  ROM #(.dataWidth(32)) rom_1 (
    .addr(counter_1_q), .data({out_14, rom_1_data[24:15], func3, rom_1_data[11:7], op_code}));  // open: sel
  assign bit_extender_1_out = {{20{1'b0}}, {out_14, rom_1_data[24:20]}};  // Bit_Extender bit_extender_1
  // Register_file_32_bits REG_FILE: pin names not known; wires that end beside it: rom_1_data[11:7], rom_1_data[24:20], value_rd, rom_1_data[19:15], clock_1_out, in_1, regWriteEnable, REG_FILE_p8, REG_FILE_p9
  Multiplexer #(.width(32), .enable("false")) multiplexer_1 (
    .in0(REG_FILE_p9), .in1(bit_extender_1_out), .out(multiplexer_1_out), .sel(B_sel));
  Bit_Extender #(.in_width(7), .out_width(1)) bit_extender_2 (.in(out_14), .out(bit_extender_2_out));

  // Notes on the sheet:
  //   contents of rom_1 (hex, n*v repeats v):
  //   500213 600293 40428333
  //   imm[20:31]
  //   value_rd
  //   rs1
  //   rs2
  //   rd
  //   value_rs1
  //   value_rs2
endmodule
