// Logisim project control op.circ as structural Verilog: 1 circuit, main circuit main
module main (
  input  [2:0] ALUOp,
  input  Func_7,
  input  [2:0] Func_3,
  output [4:0] out_4
);

  wire and_1_out, and_2_out, and_3_out, and_4_out, and_5_out, and_6_out, and_7_out, and_8_out, and_9_out,
       not_1_out, not_2_out, not_3_out, not_4_out, not_5_out, not_6_out, not_7_out, not_8_out, not_9_out,
       not_10_out, not_11_out, not_12_out, not_13_out, not_14_out, not_15_out, not_16_out;
  wire [2:0] priority_encoder_1_out;

  and and_1 (and_1_out, ALUOp[0], ALUOp[1]);
  and and_2 (and_2_out, ALUOp[1], not_1_out);
  not not_1 (not_1_out, ALUOp[0]);
  not not_2 (not_2_out, ALUOp[1]);
  not not_3 (not_3_out, ALUOp[0]);
  not not_4 (not_4_out, Func_7);
  not not_5 (not_5_out, ALUOp[0]);
  not not_6 (not_6_out, ALUOp[1]);
  not not_7 (not_7_out, ALUOp[2]);
  not not_8 (not_8_out, ALUOp[1]);
  not not_9 (not_9_out, Func_7);
  not not_10 (not_10_out, Func_3[1]);
  and and_3 (and_3_out, not_2_out, not_3_out, not_4_out);
  and and_4 (and_4_out, not_5_out, not_6_out, Func_7);
  and and_5 (and_5_out, ALUOp[0], not_7_out, not_8_out);
  and and_6 (and_6_out, not_10_out, Func_3[2], Func_3[0]);
  and and_7 (and_7_out, and_5_out, not_9_out, and_6_out);
  and and_8 (and_8_out, and_5_out, and_6_out, Func_7);
  not not_11 (not_11_out, and_8_out);
  not not_12 (not_12_out, and_7_out);
  not not_13 (not_13_out, and_4_out);
  and and_9 (and_9_out, not_11_out, not_12_out, not_13_out, not_14_out, not_15_out, not_16_out);
  not not_14 (not_14_out, and_3_out);
  not not_15 (not_15_out, and_2_out);
  not not_16 (not_16_out, and_1_out);
  Priority_Encoder priority_encoder_1 (
    .in0(and_1_out), .in1(and_2_out), .in2(and_3_out), .in4(and_4_out), .in5(and_7_out), .in6(and_8_out),
    .in7(and_9_out), .out(priority_encoder_1_out));  // open: in3, en_in, gs, en_out
  Multiplexer #(.select(3), .width(5), .enable("false")) multiplexer_1 (
    .in0({5{1'b1}}), .in1({2'b10, Func_3}), .in2({2'b00, Func_3}), .in4({2'b01, Func_3}),
    .in5({2'b00, Func_3}), .in6({2'b01, Func_3}), .in7({5{1'b0}}), .out(out_4), .sel(priority_encoder_1_out));  // open: in3
endmodule
