// Logisim project decode.circ as structural Verilog: 1 circuit, main circuit main
module main (
  input  [6:0] opcode,
  output R_format,
  output Load,
  output Store,
  output Branch,
  output I_Type,
  output JALR,
  output JAL,
  output Lui
);

  Comparator #(.width(7), .mode("unsigned")) comparator_1 (.a(7'b0110011), .b(opcode), .eq(R_format));  // open: gt, lt
  Comparator #(.width(7), .mode("unsigned")) comparator_2 (.a(opcode), .b(7'b0000011), .eq(Load));  // open: gt, lt
  Comparator #(.width(7), .mode("unsigned")) comparator_3 (.a(opcode), .b(7'b0100011), .eq(Store));  // open: gt, lt
  Comparator #(.width(7), .mode("unsigned")) comparator_4 (.a(opcode), .b(7'b1100011), .eq(Branch));  // open: gt, lt
  Comparator #(.width(7), .mode("unsigned")) comparator_5 (.a(opcode), .b(7'b0010011), .eq(I_Type));  // open: gt, lt
  Comparator #(.width(7), .mode("unsigned")) comparator_6 (.a(opcode), .b(7'b0110111), .eq(JALR));  // open: gt, lt
  Comparator #(.width(7), .mode("unsigned")) comparator_7 (.a(opcode), .b(7'b1101111), .eq(JAL));  // open: gt, lt
  Comparator #(.width(7), .mode("unsigned")) comparator_8 (.a(opcode), .b(7'b0110111), .eq(Lui));  // open: gt, lt
endmodule
